// Logisim project First.circ as structural Verilog: 3 circuits, main circuit main
module main (
  input  K,
  input  C,
  input  J,
  output Q,
  output NOTQ
);

  wire and_1_out, and_2_out, not_1_out, rsctrigger_2_notq, rsctrigger_2_q;

  and and_1 (and_1_out, rsctrigger_2_q, K);
  and and_2 (and_2_out, J, rsctrigger_2_notq);
  not not_1 (not_1_out, C);
  RSCTrigger rsctrigger_1 (.R(and_1_out), .C(C), .S(and_2_out), .Q(Q), .NOTQ(NOTQ));
  RSCTrigger rsctrigger_2 (.R(NOTQ), .C(not_1_out), .S(Q), .Q(rsctrigger_2_q), .NOTQ(rsctrigger_2_notq));
endmodule

module RSTrigger (
  input  in_1,
  input  in_2,
  output out_3,
  output out_4
);

  nor nor_1 (out_3, in_1, out_4);
  nor nor_2 (out_4, out_3, in_2);
endmodule

module RSCTrigger (
  input  R,
  input  C,
  input  S,
  output Q,
  output NOTQ
);

  wire and_1_out, and_2_out, nor_2_out, por_1_out;

  and and_1 (and_1_out, R, C);
  and and_2 (and_2_out, C, S);
  nor nor_1 (Q, and_1_out, NOTQ);
  nor nor_2 (nor_2_out, Q, and_2_out);
  POR por_1 (.out(por_1_out));
  or or_1 (NOTQ, nor_2_out, por_1_out);
endmodule
