// Logisim project counter.circ as structural Verilog: 9 circuits, main circuit main
module main (
  input  T,
  output Q0,
  output Q1,
  output Q2,
  output Q3
);

  wire mymodule_1_out_5, mytrigger_1_out_5, mytrigger_2_out_5, mytrigger_3_out_5, mytrigger_4_out_5;

  MyTrigger mytrigger_1 (.D(1'b0), .T(T), .TW(T), .W(mymodule_1_out_5), .out_5(mytrigger_1_out_5));
  MyTrigger mytrigger_2 (.D(1'b1), .T(mytrigger_1_out_5), .TW(T), .W(mymodule_1_out_5), .out_5(mytrigger_2_out_5));
  MyTrigger mytrigger_3 (.D(1'b0), .T(mytrigger_2_out_5), .TW(T), .W(mymodule_1_out_5), .out_5(mytrigger_3_out_5));
  MyTrigger mytrigger_4 (.D(1'b0), .T(mytrigger_3_out_5), .TW(T), .W(mymodule_1_out_5), .out_5(mytrigger_4_out_5));
  MyModule mymodule_1 (
    .Q0(mytrigger_1_out_5), .Q1(mytrigger_2_out_5), .Q2(mytrigger_3_out_5), .Q3(mytrigger_4_out_5),
    .out_5(mymodule_1_out_5));
  Plus plus_1 (
    .Q0(mytrigger_1_out_5), .Q1(mytrigger_2_out_5), .Q2(mytrigger_3_out_5), .Q3(mytrigger_4_out_5), .Z0(Q0),
    .Z1(Q1), .Z2(Q2), .Z3(Q3));
endmodule

module FullAdder (
  input  X,
  input  Y,
  input  C,
  output Z,
  output H
);

  xor xor_1 (Z, X, Y, C);
  Median median_1 (.X(X), .Y(Y), .Z(C), .out_4(H));
endmodule

module Median (
  input  X,
  input  Y,
  input  Z,
  output out_4
);

  wire and_1_out, and_2_out, and_3_out;

  and and_1 (and_1_out, X, Y);
  and and_2 (and_2_out, X, Z);
  and and_3 (and_3_out, Y, Z);
  or or_1 (out_4, and_1_out, and_2_out, and_3_out);
endmodule

module RSCTrigger (
  input  R,
  input  C,
  input  S,
  output Q,
  output NOTQ
);

  wire and_1_out, and_2_out, nor_2_out, por_1_out;

  and and_1 (and_1_out, R, C);
  and and_2 (and_2_out, C, S);
  nor nor_1 (Q, and_1_out, NOTQ);
  nor nor_2 (nor_2_out, Q, and_2_out);
  POR por_1 (.out(por_1_out));
  or or_1 (NOTQ, nor_2_out, por_1_out);
endmodule

module Plus (
  input  Q0,
  input  Q1,
  input  Q2,
  input  Q3,
  output Z0,
  output Z1,
  output Z2,
  output Z3
);

  wire fulladder_1_h, fulladder_1_z, fulladder_2_h, fulladder_2_z, fulladder_3_h, fulladder_3_z,
       fulladder_4_z, nand_1_out, xor_1_out, xor_2_out, xor_3_out, xor_4_out;

  xor xor_1 (xor_1_out, Q0, 1'b1);
  xor xor_2 (xor_2_out, Q1, 1'b1);
  xor xor_3 (xor_3_out, Q2, 1'b1);
  xor xor_4 (xor_4_out, Q3, 1'b1);
  nand nand_1 (nand_1_out, xor_1_out, xor_2_out, xor_3_out, xor_4_out);
  FullAdder fulladder_1 (.X(Q0), .Y(1'b1), .C(1'b0), .Z(fulladder_1_z), .H(fulladder_1_h));
  FullAdder fulladder_2 (.X(Q1), .Y(1'b1), .C(fulladder_1_h), .Z(fulladder_2_z), .H(fulladder_2_h));
  FullAdder fulladder_3 (.X(Q2), .Y(1'b1), .C(fulladder_2_h), .Z(fulladder_3_z), .H(fulladder_3_h));
  FullAdder fulladder_4 (.X(Q3), .Y(1'b1), .C(fulladder_3_h), .Z(fulladder_4_z));  // open: H
  and and_1 (Z0, nand_1_out, fulladder_1_z);
  and and_2 (Z1, nand_1_out, fulladder_2_z);
  and and_3 (Z2, nand_1_out, fulladder_3_z);
  and and_4 (Z3, nand_1_out, fulladder_4_z);
endmodule

module JKTrigger (
  input  K,
  input  C,
  input  J,
  output Q,
  output NOTQ
);

  wire and_1_out, and_2_out, not_1_out, rsctrigger_1_notq, rsctrigger_1_q;

  and and_1 (and_1_out, Q, K);
  and and_2 (and_2_out, J, NOTQ);
  not not_1 (not_1_out, C);
  RSCTrigger rsctrigger_1 (.R(and_1_out), .C(C), .S(and_2_out), .Q(rsctrigger_1_q), .NOTQ(rsctrigger_1_notq));
  RSCTrigger rsctrigger_2 (.R(rsctrigger_1_notq), .C(not_1_out), .S(rsctrigger_1_q), .Q(Q), .NOTQ(NOTQ));
endmodule

module MyModule (
  input  Q0,
  input  Q1,
  input  Q2,
  input  Q3,
  output out_5
);

  nor nor_1 (out_5, Q0, Q1, Q2, Q3);
endmodule

module Mult (
  input  C0,
  input  C1,
  input  Q,
  output out_4
);

  wire and_1_out, and_2_out, not_1_out;

  not not_1 (not_1_out, Q);
  and and_1 (and_1_out, C0, not_1_out);
  and and_2 (and_2_out, C1, Q);
  or or_1 (out_4, and_1_out, and_2_out);
endmodule

module MyTrigger (
  input  D,
  input  T,
  input  TW,
  input  W,
  output out_5
);

  wire jktrigger_1_notq, mult_1_out_4, mult_2_out_4, not_1_out;

  Mult mult_1 (.C0(jktrigger_1_notq), .C1(D), .Q(W), .out_4(mult_1_out_4));
  Mult mult_2 (.C0(T), .C1(TW), .Q(W), .out_4(mult_2_out_4));
  not not_1 (not_1_out, mult_1_out_4);
  JKTrigger jktrigger_1 (.K(not_1_out), .C(mult_2_out_4), .J(mult_1_out_4), .Q(out_5), .NOTQ(jktrigger_1_notq));
endmodule
