// Logisim project lfsr.circ as structural Verilog: 4 circuits, main circuit main
module main (
  input  POR,
  input  T,
  output out_3
);

  wire or_1_out, or_2_out, Q1_out_3, Q2_out_3, Q3_out_3, Q4_out_3, Q5_out_3, Q6_out_3, Q7_out_3, Q8_out_3,
       Q9_out_3, Q10_out_3, Q11_out_3, Q12_out_3, xor_1_out, xor_2_out, xor_3_out, xor_4_out;

  or or_1 (or_1_out, POR, xor_1_out);
  or or_2 (or_2_out, POR, T);
  MyTrigger Q0 (.D(or_1_out), .T(or_2_out), .out_3(out_3));
  MyTrigger Q1 (.D(Q2_out_3), .T(T), .out_3(Q1_out_3));
  MyTrigger Q2 (.D(Q3_out_3), .T(T), .out_3(Q2_out_3));
  MyTrigger Q3 (.D(xor_2_out), .T(T), .out_3(Q3_out_3));
  MyTrigger Q4 (.D(Q5_out_3), .T(T), .out_3(Q4_out_3));
  MyTrigger Q5 (.D(xor_3_out), .T(T), .out_3(Q5_out_3));
  MyTrigger Q6 (.D(Q7_out_3), .T(T), .out_3(Q6_out_3));
  MyTrigger Q7 (.D(Q8_out_3), .T(T), .out_3(Q7_out_3));
  MyTrigger Q8 (.D(Q9_out_3), .T(T), .out_3(Q8_out_3));
  MyTrigger Q9 (.D(Q10_out_3), .T(T), .out_3(Q9_out_3));
  MyTrigger Q10 (.D(Q11_out_3), .T(T), .out_3(Q10_out_3));
  MyTrigger Q11 (.D(xor_4_out), .T(T), .out_3(Q11_out_3));
  MyTrigger Q12 (.D(out_3), .T(T), .out_3(Q12_out_3));
  xor xor_1 (xor_1_out, out_3, Q1_out_3);
  xor xor_2 (xor_2_out, out_3, Q4_out_3);
  xor xor_3 (xor_3_out, out_3, Q6_out_3);
  xor xor_4 (xor_4_out, out_3, Q12_out_3);
endmodule

module RSCTrigger (
  input  R,
  input  C,
  input  S,
  output Q,
  output NOTQ
);

  wire and_1_out, and_2_out, nor_2_out, por_1_out;

  and and_1 (and_1_out, R, C);
  and and_2 (and_2_out, C, S);
  nor nor_1 (Q, and_1_out, NOTQ);
  nor nor_2 (nor_2_out, Q, and_2_out);
  POR por_1 (.out(por_1_out));
  or or_1 (NOTQ, nor_2_out, por_1_out);
endmodule

module JKTrigger (
  input  K,
  input  C,
  input  J,
  output Q,
  output NOTQ
);

  wire and_1_out, and_2_out, not_1_out, rsctrigger_1_notq, rsctrigger_1_q;

  and and_1 (and_1_out, Q, K);
  and and_2 (and_2_out, J, NOTQ);
  not not_1 (not_1_out, C);
  RSCTrigger rsctrigger_1 (.R(and_1_out), .C(C), .S(and_2_out), .Q(rsctrigger_1_q), .NOTQ(rsctrigger_1_notq));
  RSCTrigger rsctrigger_2 (.R(rsctrigger_1_notq), .C(not_1_out), .S(rsctrigger_1_q), .Q(Q), .NOTQ(NOTQ));
endmodule

module MyTrigger (
  input  D,
  input  T,
  output out_3
);

  wire not_1_out;

  not not_1 (not_1_out, D);
  JKTrigger jktrigger_1 (.K(not_1_out), .C(T), .J(D), .Q(out_3));  // open: NOTQ
endmodule
